// Logisim project branch-comp.circ as structural Verilog: 1 circuit, main circuit branch_comp
module branch_comp (
  input  [31:0] BrData1,
  input  [31:0] BrData2,
  input  BrUn,
  output BrEq,
  output BrLt
);

  wire BrLtS, BrLtS1, BrLtS2, BrLtU, SignDiff;

  Comparator #(.width(32)) comparator_1 (.a(BrData1), .b(BrData2), .eq(BrEq));  // open: gt, lt
  Comparator #(.mode("unsigned"), .width(32)) comparator_2 (.a(BrData1), .b(BrData2), .lt(BrLtU));  // open: gt, eq
  xor xor_1 (SignDiff, BrData1[31], BrData2[31]);
  Comparator #(.width(31)) comparator_3 (.a(BrData1[30:0]), .b(BrData2[30:0]), .lt(BrLtS1));  // open: gt, eq
  Comparator #(.width(1)) comparator_4 (.a(BrData1[31]), .b(1'b1), .eq(BrLtS2));  // open: gt, lt
  Multiplexer multiplexer_1 (.in0(BrLtS1), .in1(BrLtS2), .out(BrLtS), .sel(SignDiff));
  Multiplexer multiplexer_2 (.in0(BrLtS), .in1(BrLtU), .out(BrLt), .sel(BrUn));

  // Other names for the same wires on the sheet: Rest1[30:0] = BrData1[30:0]; Sign1 = BrData1[31];
  //   Rest2[30:0] = BrData2[30:0]; Sign2 = BrData2[31]

  // Notes on the sheet:
  //   INPUTS to your circuit
  //   DON'T CHANGE THE LOCATIONS OF THE INPUTS AND OUTPUTS!
  //   OUTPUT from your circuit
endmodule
