// Logisim project control-logic.circ as structural Verilog: 1 circuit, main circuit control_logic
module control_logic (
  input  [31:0] Instruction,
  input  BrEq,
  input  BrLt,
  output PCSel,
  output RegWEn,
  output [2:0] ImmSel,
  output BrUn,
  output ASel,
  output BSel,
  output [3:0] ALUSel,
  output MemRW,
  output [1:0] WBSel
);

  wire and_10_out, and_11_out, and_29_out, and_30_out, and_31_out, and_32_out, and_33_out, and_34_out, B,
       comparator_1_eq, comparator_2_eq, comparator_3_eq, comparator_4_eq, comparator_5_eq, comparator_6_eq,
       comparator_7_eq, comparator_8_eq, comparator_9_eq, comparator_10_eq, comparator_11_eq,
       comparator_12_eq, comparator_13_eq, comparator_14_eq, comparator_15_eq, comparator_16_eq,
       comparator_17_eq, comparator_18_eq, comparator_19_eq, comparator_20_eq, comparator_21_eq,
       comparator_31_eq, comparator_32_eq, comparator_33_eq, comparator_34_eq, comparator_35_eq,
       comparator_36_eq, comparator_37_eq, comparator_38_eq, comparator_39_eq, comparator_40_eq,
       comparator_41_eq, comparator_42_eq, comparator_43_eq, comparator_44_eq, comparator_45_eq,
       comparator_46_eq, I_ALU, I_loads, is_add, is_addi, is_and, is_andi, is_auipc, is_beq, is_bge, is_bgeu,
       is_blt, is_bltu, is_bne, is_jal, is_jalr, is_LB, is_LH, is_lui, is_LW, is_mul, is_mulh, is_mulhu,
       is_or, is_ori, is_sb, is_sh, is_sll, is_slli, is_slt, is_slti, is_sra, is_srai, is_srl, is_srli,
       is_sub, is_sw, is_xor, is_xori, not_1_out, not_2_out, not_3_out, or_1_out, or_2_out, or_3_out,
       or_4_out, or_5_out, or_6_out, R, S, Sect1, Sect2, Sect3;
  wire [5:0] ROM_in;
  wire [15:14] rom_1_data;

  Comparator #(.width(3)) comparator_1 (.a(Instruction[14:12]), .b(3'b000), .eq(comparator_1_eq));  // open: gt, lt
  Comparator #(.width(3)) comparator_2 (.a(Instruction[14:12]), .b(3'b001), .eq(comparator_2_eq));  // open: gt, lt
  Comparator #(.width(3)) comparator_3 (.a(Instruction[14:12]), .b(3'b010), .eq(comparator_3_eq));  // open: gt, lt
  Comparator #(.width(3)) comparator_4 (.a(Instruction[14:12]), .b(3'b000), .eq(comparator_4_eq));  // open: gt, lt
  Comparator #(.width(3)) comparator_5 (.a(Instruction[14:12]), .b(3'b001), .eq(comparator_5_eq));  // open: gt, lt
  Comparator #(.width(3)) comparator_6 (.a(Instruction[14:12]), .b(3'b010), .eq(comparator_6_eq));  // open: gt, lt
  Comparator #(.width(3)) comparator_7 (.a(Instruction[14:12]), .b(3'b100), .eq(comparator_7_eq));  // open: gt, lt
  Comparator #(.width(3)) comparator_8 (.a(Instruction[14:12]), .b(3'b110), .eq(comparator_8_eq));  // open: gt, lt
  Comparator #(.width(3)) comparator_9 (.a(Instruction[14:12]), .b(3'b111), .eq(comparator_9_eq));  // open: gt, lt
  Comparator #(.width(3)) comparator_10 (.a(Instruction[14:12]), .b(3'b101), .eq(comparator_10_eq));  // open: gt, lt
  Comparator #(.width(7)) comparator_11 (.a(Instruction[31:25]), .b({7{1'b0}}), .eq(comparator_11_eq));  // open: gt, lt
  Comparator #(.width(3)) comparator_12 (.a(Instruction[14:12]), .b(3'b101), .eq(comparator_12_eq));  // open: gt, lt
  Comparator #(.width(7)) comparator_13 (
    .a(Instruction[31:25]), .b(7'b0100000), .eq(comparator_13_eq));  // open: gt, lt
  ROM #(.addrWidth(6), .dataWidth(16)) rom_1 (
    .addr(ROM_in), .data({rom_1_data, WBSel, MemRW, ALUSel, BSel, ASel, BrUn, ImmSel, RegWEn}));
  and and_1 (is_LB, comparator_1_eq, I_loads);
  and and_2 (is_LH, comparator_2_eq, I_loads);
  and and_3 (is_LW, comparator_3_eq, I_loads);
  and and_4 (is_addi, comparator_4_eq, I_ALU);
  and and_5 (is_slli, comparator_5_eq, I_ALU);
  and and_6 (is_slti, comparator_6_eq, I_ALU);
  and and_7 (is_xori, comparator_7_eq, I_ALU);
  and and_8 (is_ori, comparator_8_eq, I_ALU);
  and and_9 (is_andi, comparator_9_eq, I_ALU);
  and and_10 (and_10_out, comparator_10_eq, I_ALU);
  and and_11 (and_11_out, comparator_12_eq, I_ALU);
  and and_12 (is_srli, and_10_out, comparator_11_eq);
  and and_13 (is_srai, and_11_out, comparator_13_eq);
  Comparator #(.width(3)) comparator_14 (.a(Instruction[14:12]), .b(3'b000), .eq(comparator_14_eq));  // open: gt, lt
  Comparator #(.width(3)) comparator_15 (.a(Instruction[14:12]), .b(3'b001), .eq(comparator_15_eq));  // open: gt, lt
  Comparator #(.width(3)) comparator_16 (.a(Instruction[14:12]), .b(3'b011), .eq(comparator_16_eq));  // open: gt, lt
  Comparator #(.width(3)) comparator_17 (.a(Instruction[14:12]), .b(3'b010), .eq(comparator_17_eq));  // open: gt, lt
  Comparator #(.width(3)) comparator_18 (.a(Instruction[14:12]), .b(3'b100), .eq(comparator_18_eq));  // open: gt, lt
  Comparator #(.width(3)) comparator_19 (.a(Instruction[14:12]), .b(3'b101), .eq(comparator_19_eq));  // open: gt, lt
  Comparator #(.width(3)) comparator_20 (.a(Instruction[14:12]), .b(3'b110), .eq(comparator_20_eq));  // open: gt, lt
  Comparator #(.width(3)) comparator_21 (.a(Instruction[14:12]), .b(3'b111), .eq(comparator_21_eq));  // open: gt, lt
  and and_14 (Sect1, comparator_14_eq, R);
  and and_15 (Sect2, comparator_15_eq, R);
  and and_16 (is_mulhu, comparator_16_eq, R);
  and and_17 (is_slt, comparator_17_eq, R);
  and and_18 (is_xor, comparator_18_eq, R);
  and and_19 (Sect3, comparator_19_eq, R);
  and and_20 (is_or, comparator_20_eq, R);
  and and_21 (is_and, comparator_21_eq, R);
  Comparator #(.width(7)) comparator_22 (.a(Instruction[6:0]), .b(7'b0110011), .eq(R));  // open: gt, lt
  Comparator #(.width(7)) comparator_23 (.a(Instruction[6:0]), .b(7'b0100011), .eq(S));  // open: gt, lt
  Comparator #(.width(7)) comparator_24 (.a(Instruction[6:0]), .b(7'b1100011), .eq(B));  // open: gt, lt
  Comparator #(.width(7)) comparator_25 (.a(Instruction[6:0]), .b(7'b0000011), .eq(I_loads));  // open: gt, lt
  Comparator #(.width(7)) comparator_26 (.a(Instruction[6:0]), .b(7'b0010011), .eq(I_ALU));  // open: gt, lt
  Comparator #(.width(7)) comparator_27 (.a(Instruction[6:0]), .b(7'b1100111), .eq(is_jalr));  // open: gt, lt
  Comparator #(.width(7)) comparator_28 (.a(Instruction[6:0]), .b(7'b0010111), .eq(is_auipc));  // open: gt, lt
  Comparator #(.width(7)) comparator_29 (.a(Instruction[6:0]), .b(7'b0110111), .eq(is_lui));  // open: gt, lt
  Comparator #(.width(7)) comparator_30 (.a(Instruction[6:0]), .b(7'b1101111), .eq(is_jal));  // open: gt, lt
  Comparator #(.width(7)) comparator_31 (.a(Instruction[31:25]), .b({7{1'b0}}), .eq(comparator_31_eq));  // open: gt, lt
  Comparator #(.width(7)) comparator_32 (
    .a(Instruction[31:25]), .b(7'b0000001), .eq(comparator_32_eq));  // open: gt, lt
  Comparator #(.width(7)) comparator_33 (
    .a(Instruction[31:25]), .b(7'b0100000), .eq(comparator_33_eq));  // open: gt, lt
  Comparator #(.width(7)) comparator_34 (
    .a(Instruction[31:25]), .b(7'b0000001), .eq(comparator_34_eq));  // open: gt, lt
  Comparator #(.width(7)) comparator_35 (.a(Instruction[31:25]), .b({7{1'b0}}), .eq(comparator_35_eq));  // open: gt, lt
  Comparator #(.width(7)) comparator_36 (.a(Instruction[31:25]), .b({7{1'b0}}), .eq(comparator_36_eq));  // open: gt, lt
  Comparator #(.width(7)) comparator_37 (
    .a(Instruction[31:25]), .b(7'b0100000), .eq(comparator_37_eq));  // open: gt, lt
  and and_22 (is_add, Sect1, comparator_31_eq);
  and and_23 (is_mul, Sect1, comparator_32_eq);
  and and_24 (is_sub, Sect1, comparator_33_eq);
  and and_25 (is_mulh, Sect2, comparator_34_eq);
  and and_26 (is_sll, Sect2, comparator_35_eq);
  and and_27 (is_srl, Sect3, comparator_36_eq);
  and and_28 (is_sra, Sect3, comparator_37_eq);
  not not_1 (not_1_out, BrEq);
  not not_2 (not_2_out, BrLt);
  not not_3 (not_3_out, BrLt);
  Comparator #(.width(3)) comparator_38 (.a(Instruction[14:12]), .b(3'b000), .eq(comparator_38_eq));  // open: gt, lt
  Comparator #(.width(3)) comparator_39 (.a(Instruction[14:12]), .b(3'b001), .eq(comparator_39_eq));  // open: gt, lt
  Comparator #(.width(3)) comparator_40 (.a(Instruction[14:12]), .b(3'b100), .eq(comparator_40_eq));  // open: gt, lt
  Comparator #(.width(3)) comparator_41 (.a(Instruction[14:12]), .b(3'b101), .eq(comparator_41_eq));  // open: gt, lt
  Comparator #(.width(3)) comparator_42 (.a(Instruction[14:12]), .b(3'b110), .eq(comparator_42_eq));  // open: gt, lt
  Comparator #(.width(3)) comparator_43 (.a(Instruction[14:12]), .b(3'b111), .eq(comparator_43_eq));  // open: gt, lt
  and and_29 (and_29_out, is_beq, BrEq);
  and and_30 (and_30_out, is_bne, not_1_out);
  and and_31 (and_31_out, is_blt, BrLt);
  and and_32 (and_32_out, is_bltu, BrLt);
  and and_33 (and_33_out, is_bge, not_2_out);
  and and_34 (and_34_out, is_bgeu, not_3_out);
  and and_35 (is_beq, comparator_38_eq, B);
  and and_36 (is_bne, comparator_39_eq, B);
  and and_37 (is_blt, comparator_40_eq, B);
  and and_38 (is_bge, comparator_41_eq, B);
  and and_39 (is_bltu, comparator_42_eq, B);
  and and_40 (is_bgeu, comparator_43_eq, B);
  or or_1 (or_1_out, and_29_out, and_30_out);
  or or_2 (or_2_out, and_31_out, and_32_out);
  or or_3 (or_3_out, and_33_out, and_34_out);
  or or_4 (or_4_out, or_1_out, or_2_out);
  Comparator #(.width(3)) comparator_44 (.a(Instruction[14:12]), .b(3'b000), .eq(comparator_44_eq));  // open: gt, lt
  Comparator #(.width(3)) comparator_45 (.a(Instruction[14:12]), .b(3'b001), .eq(comparator_45_eq));  // open: gt, lt
  Comparator #(.width(3)) comparator_46 (.a(Instruction[14:12]), .b(3'b010), .eq(comparator_46_eq));  // open: gt, lt
  or or_5 (or_5_out, or_4_out, or_3_out);
  and and_41 (is_sb, comparator_44_eq, S);
  and and_42 (is_sh, comparator_45_eq, S);
  and and_43 (is_sw, comparator_46_eq, S);
  or or_6 (or_6_out, or_5_out, is_jal);
  or or_7 (PCSel, or_6_out, is_jalr);
  Priority_Encoder #(.select_enc(6)) priority_encoder_1 (
    .in0(is_add), .in1(is_mul), .in2(is_sub), .in3(is_sll), .in4(is_mulh), .in5(is_mulhu), .in6(is_slt),
    .in7(is_xor), .in8(is_srl), .in9(is_sra), .in10(is_or), .in11(is_and), .in12(is_LB), .in13(is_LH),
    .in14(is_LW), .in15(is_addi), .in16(is_slli), .in17(is_slti), .in18(is_xori), .in19(is_srli),
    .in20(is_srai), .in21(is_ori), .in22(is_andi), .in23(is_sb), .in24(is_sh), .in25(is_sw), .in26(is_beq),
    .in27(is_bne), .in28(is_blt), .in29(is_bge), .in30(is_bltu), .in31(is_bgeu), .in32(is_auipc),
    .in33(is_lui), .in34(is_jal), .in35(is_jalr), .in36(1'b0), .in37(1'b0), .in38(1'b0), .in39(1'b0),
    .in40(1'b0), .in41(1'b0), .in42(1'b0), .in43(1'b0), .in44(1'b0), .in45(1'b0), .in46(1'b0), .in47(1'b0),
    .in48(1'b0), .in49(1'b0), .in50(1'b0), .in51(1'b0), .in52(1'b0), .in53(1'b0), .in54(1'b0), .in55(1'b0),
    .in56(1'b0), .in57(1'b0), .in58(1'b0), .in59(1'b0), .in60(1'b0), .in61(1'b0), .in62(1'b0), .in63(1'b0),
    .out(ROM_in));  // open: gs, en_out, en_in

  // Other names for the same wires on the sheet: Opcode[6:0] = Instruction[6:0];
  //   Rest[14:0] = {Instruction[24:15], Instruction[11:7]}; Func3[2:0] = Instruction[14:12];
  //   Func7[6:0] = Instruction[31:25]

  // Notes on the sheet:
  //   INPUTS to your circuit
  //   Connect ROM Input here ->
  //   contents of rom_1 (hex, n*v repeats v):
  //   1001 1401 1601 1081 1481 1581 1101 1201 1281 1681 1301 1381 41 41 41 1041 10c1 1141 1241 12c1 16c1
  //   1341 13c1 842 842 842 4*64 74 74 1067 17c7 2069 2041
  //   ROM FOR CONTROL LOGIC
  //   DON'T CHANGE THE LOCATIONS OF THE INPUTS AND OUTPUTS!
  //   This is only if you choose to do the ROM option
  //   CONNECT
  //   WIRE
  //   TO
  //   USE
  //   ROM
  //   OUTPUT from your circuit
  //   Reminder: If using ROM, use combinational logic for PCSel
endmodule
