// Logisim project cpu.circ as structural Verilog: 1 circuit, main circuit cpu
module cpu (
  input  clk,
  input  [31:0] Instruction,
  input  [31:0] MemReadData,
  output [31:0] MemAddress,
  output [31:0] ProgramCounter,
  output [31:0] ra,
  output [31:0] sp,
  output [31:0] t0,
  output [31:0] t1,
  output [31:0] t2,
  output [31:0] s0,
  output [31:0] s1,
  output [31:0] a0,
  output [3:0] MemWriteMask,
  output [31:0] MemWriteData
);

  wire ASel, BrEq, BrLt, BrUn, BSel, MemRW, PCSel, RegWEn;
  wire [1:0] WBSel;
  wire [2:0] ImmSel;
  wire [3:0] ALUSel;
  wire [4:0] RD, RS1, RS2;
  wire [6:0] Stage1_Instruction;
  wire [9:0] Rest;
  wire [31:0] adder_1_out, imm_gen_1_immediate, multiplexer_1_out, multiplexer_2_out, multiplexer_3_out,
       multiplexer_4_out, multiplexer_5_out, partial_load_1_datatoreg, PC4, regfile_1_readdata1, RS2_data,
       Stage1_PC;

  Adder #(.width(32)) adder_1 (.a(ProgramCounter), .b(32'h4), .out(adder_1_out));  // open: cin, cout
  Register #(.width(32)) PC (.D(multiplexer_1_out), .clk(clk), .Q(ProgramCounter));  // open: en, clr
  Multiplexer #(.width(32)) multiplexer_1 (.in0(adder_1_out), .in1(MemAddress), .out(multiplexer_1_out), .sel(PCSel));
  Register #(.width(32)) Instruction_Reg (
    .D(multiplexer_2_out), .clk(clk), .Q({Rest[9:3], RS2, RS1, Rest[2:0], RD, Stage1_Instruction}));  // open: en, clr
  Multiplexer #(.width(32)) multiplexer_2 (.in0(Instruction), .in1(32'h13), .out(multiplexer_2_out), .sel(PCSel));
  Register #(.width(32)) PC_Reg (.D(ProgramCounter), .clk(clk), .Q(Stage1_PC));  // open: en, clr
  control_logic control_logic_1 (
    .Instruction({Rest[9:3], RS2, RS1, Rest[2:0], RD, Stage1_Instruction}), .BrEq(BrEq), .BrLt(BrLt),
    .PCSel(PCSel), .RegWEn(RegWEn), .ImmSel(ImmSel), .BrUn(BrUn), .ASel(ASel), .BSel(BSel), .ALUSel(ALUSel),
    .MemRW(MemRW), .WBSel(WBSel));
  regfile regfile_1 (
    .ReadIndex1(RS1), .ReadIndex2(RS2), .WriteIndex(RD), .WriteData(multiplexer_5_out), .RegWEn(RegWEn),
    .clk(clk), .ra(ra), .sp(sp), .t0(t0), .t1(t1), .t2(t2), .s0(s0), .s1(s1), .a0(a0),
    .ReadData1(regfile_1_readdata1), .ReadData2(RS2_data));
  imm_gen imm_gen_1 (
    .Instruction({Rest[9:3], RS2, RS1, Rest[2:0], RD, Stage1_Instruction}), .ImmSel(ImmSel),
    .Immediate(imm_gen_1_immediate));
  Multiplexer #(.width(32)) multiplexer_3 (
    .in0(RS2_data), .in1(imm_gen_1_immediate), .out(multiplexer_3_out), .sel(BSel));
  branch_comp branch_comp_1 (.BrData1(regfile_1_readdata1), .BrData2(RS2_data), .BrUn(BrUn), .BrEq(BrEq), .BrLt(BrLt));
  Multiplexer #(.width(32)) multiplexer_4 (
    .in0(regfile_1_readdata1), .in1(Stage1_PC), .out(multiplexer_4_out), .sel(ASel));
  alu alu_1 (.A(multiplexer_4_out), .B(multiplexer_3_out), .ALUSel(ALUSel), .ALUResult(MemAddress));
  partial_load partial_load_1 (
    .Instruction({Rest[9:3], RS2, RS1, Rest[2:0], RD, Stage1_Instruction}), .MemAddress(MemAddress),
    .DataFromMem(MemReadData), .DataToReg(partial_load_1_datatoreg));
  partial_store partial_store_1 (
    .Instruction({Rest[9:3], RS2, RS1, Rest[2:0], RD, Stage1_Instruction}), .MemAddress(MemAddress),
    .DataFromReg(RS2_data), .MemRW(MemRW), .MemWriteMask(MemWriteMask), .DataToMem(MemWriteData));
  Multiplexer #(.select(2), .width(32)) multiplexer_5 (
    .in0(partial_load_1_datatoreg), .in1(MemAddress), .in2(PC4), .out(multiplexer_5_out), .sel(WBSel));  // open: in3
  Adder #(.width(32)) adder_2 (.a(Stage1_PC), .b(32'h4), .out(PC4));  // open: cin, cout

  // Other names for the same wires on the sheet: Stage1_Instruction[31:7] = {Rest[9:3], RS2, RS1, Rest[2:0], RD}

  // Notes on the sheet:
  //   To IMEM
  //   IMEM (do **NOT** move this)
  //   From IMEM
  //   Inputs/Outputs for testing. Do **NOT** move these.
  //   It is OK to move the PC, RegFile, ALU, MEM, Branch Comp, Imm Gen, Partial Load, Partial Store and Control Logic to wherever is most convenient for you when constructing your CPU, and to delete this text
  //   To DMEM
  //   DMEM (do **NOT** move this)
  //   From DMEM
endmodule
