// Logisim project imm-gen.circ as structural Verilog: 1 circuit, main circuit imm_gen
module imm_gen (
  input  [31:0] Instruction,
  input  [2:0] ImmSel,
  output [31:0] Immediate
);

  wire [31:0] Immediate_B, Immediate_I, Immediate_J, Immediate_S;

  assign Immediate_I = {{20{Instruction[31]}}, Instruction[31:20]};  // Bit_Extender bit_extender_1
  assign Immediate_B = {{19{Instruction[31]}}, {Instruction[31], Instruction[7], Instruction[30:25], Instruction[11:8], 1'b0}};  // Bit_Extender bit_extender_2
  assign Immediate_S = {{20{Instruction[31]}}, {Instruction[31:25], Instruction[11:7]}};  // Bit_Extender bit_extender_3
  assign Immediate_J = {{11{Instruction[31]}}, {Instruction[31], Instruction[19:12], Instruction[20], Instruction[30:21], 1'b0}};  // Bit_Extender bit_extender_4
  Multiplexer #(.select(3), .width(32)) multiplexer_1 (
    .in0(Immediate_I), .in1(Immediate_S), .in2(Immediate_B), .in3({Instruction[31:12], {12{1'b0}}}),
    .in4(Immediate_J), .out(Immediate), .sel(ImmSel));  // open: in5, in6, in7

  // Other names for the same wires on the sheet: Immediate_U[31:12] = Instruction[31:12];
  //   J_unext[20:1] = {Instruction[31], Instruction[19:12], Instruction[20], Instruction[30:21]};
  //   part4_j[7:0] = Instruction[19:12]; twenty_imm[19:0] = Instruction[31:12]; part3_j = Instruction[20];
  //   Twelve_Imm[11:0] = Instruction[31:20]; part2_j[9:0] = Instruction[30:21];
  //   B_unext[12:1] = {Instruction[31], Instruction[7], Instruction[30:25], Instruction[11:8]};
  //   part2_b[5:0] = Instruction[30:25]; part2_s[5:0] = Instruction[30:25];
  //   S_unext[11:0] = {Instruction[31:25], Instruction[11:7]}; part1_b = Instruction[31]; part1_j = Instruction[31];
  //   part1_s = Instruction[31]; part4_b = Instruction[7]; part4_s = Instruction[7]; part3_b[3:0] = Instruction[11:8];
  //   part3_s[3:0] = Instruction[11:8]

  // Notes on the sheet:
  //   INPUTS to your circuit
  //   DON'T CHANGE THE LOCATIONS OF THE INPUTS AND OUTPUTS!
  //   OUTPUT from your circuit
endmodule
