// Logisim project partial-load.circ as structural Verilog: 1 circuit, main circuit partial_load
module partial_load (
  input  [31:0] Instruction,
  input  [31:0] MemAddress,
  input  [31:0] DataFromMem,
  output [31:0] DataToReg
);

  wire comparator_1_eq, comparator_2_eq, comparator_3_eq, comparator_4_eq, comparator_5_eq, comparator_6_eq,
       is_lb, is_lh, is_lw;
  wire [7:0] multiplexer_1_out;
  wire [15:0] multiplexer_2_out, undriven;
  wire [31:0] lb_result, lh_result, multiplexer_3_out, multiplexer_4_out;

  Multiplexer #(.select(2), .width(8)) multiplexer_1 (
    .in0(DataFromMem[7:0]), .in1(DataFromMem[15:8]), .in2(DataFromMem[23:16]), .in3(DataFromMem[31:24]),
    .out(multiplexer_1_out), .sel(MemAddress[1:0]));
  Multiplexer #(.select(2), .width(16)) multiplexer_2 (
    .in0(DataFromMem[15:0]), .in1(DataFromMem[23:8]), .in2(DataFromMem[31:16]), .in3(undriven),
    .out(multiplexer_2_out), .sel(MemAddress[1:0]));
  Comparator #(.width(7)) comparator_1 (.a(7'b0000011), .b(Instruction[6:0]), .eq(comparator_1_eq));  // open: gt, lt
  Comparator #(.width(3)) comparator_2 (.a(3'b000), .b(Instruction[14:12]), .eq(comparator_2_eq));  // open: gt, lt
  Comparator #(.width(7)) comparator_3 (.a(7'b0000011), .b(Instruction[6:0]), .eq(comparator_3_eq));  // open: gt, lt
  Comparator #(.width(3)) comparator_4 (.a(3'b001), .b(Instruction[14:12]), .eq(comparator_4_eq));  // open: gt, lt
  Comparator #(.width(7)) comparator_5 (.a(7'b0000011), .b(Instruction[6:0]), .eq(comparator_5_eq));  // open: gt, lt
  Comparator #(.width(3)) comparator_6 (.a(3'b010), .b(Instruction[14:12]), .eq(comparator_6_eq));  // open: gt, lt
  Multiplexer #(.width(32)) multiplexer_3 (.in0({32{1'b0}}), .in1(lb_result), .out(multiplexer_3_out), .sel(is_lb));
  and and_1 (is_lb, comparator_1_eq, comparator_2_eq);
  and and_2 (is_lh, comparator_3_eq, comparator_4_eq);
  and and_3 (is_lw, comparator_5_eq, comparator_6_eq);
  assign lb_result = {{24{multiplexer_1_out[7]}}, multiplexer_1_out};  // Bit_Extender bit_extender_1
  assign lh_result = {{16{multiplexer_2_out[15]}}, multiplexer_2_out};  // Bit_Extender bit_extender_2
  Multiplexer #(.width(32)) multiplexer_4 (
    .in0(multiplexer_3_out), .in1(lh_result), .out(multiplexer_4_out), .sel(is_lh));
  Multiplexer #(.width(32)) multiplexer_5 (.in0(multiplexer_4_out), .in1(DataFromMem), .out(DataToReg), .sel(is_lw));

  // Other names for the same wires on the sheet: Byte0[7:0] = DataFromMem[7:0]; Half0[15:0] = DataFromMem[15:0];
  //   Byte1[7:0] = DataFromMem[15:8]; Half1[15:0] = DataFromMem[23:8]; Byte2[7:0] = DataFromMem[23:16];
  //   Half2[15:0] = DataFromMem[31:16]; Byte3[7:0] = DataFromMem[31:24]; Opcode[6:0] = Instruction[6:0];
  //   Func3[2:0] = Instruction[14:12]; Bottom2[1:0] = MemAddress[1:0]

  // Notes on the sheet:
  //   INPUTS to your circuit
  //   DON'T CHANGE THE LOCATIONS OF THE INPUTS AND OUTPUTS!
  //   OUTPUT from your circuit
endmodule
