// Logisim project partial-store.circ as structural Verilog: 1 circuit, main circuit partial_store
module partial_store (
  input  [31:0] Instruction,
  input  [31:0] MemAddress,
  input  [31:0] DataFromReg,
  input  MemRW,
  output [3:0] MemWriteMask,
  output [31:0] DataToMem
);

  wire comparator_1_eq, comparator_2_eq, comparator_3_eq, comparator_4_eq, comparator_5_eq, comparator_6_eq,
       is_sb, is_sh, is_sw;
  wire [3:0] multiplexer_2_out, multiplexer_6_out, sb_mask, sh_mask;
  wire [31:0] bit_extender_1_out, bit_extender_2_out, Data_SB, Data_SH, multiplexer_1_out, multiplexer_5_out,
       shifter_1_out, shifter_2_out, shifter_3_out, shifter_4_out;

  Multiplexer #(.width(32)) multiplexer_1 (.in0({32{1'b0}}), .in1(Data_SB), .out(multiplexer_1_out), .sel(is_sb));
  Multiplexer #(.width(4)) multiplexer_2 (.in0(4'b0000), .in1(sb_mask), .out(multiplexer_2_out), .sel(is_sb));
  assign bit_extender_1_out = {{16{1'b0}}, DataFromReg[15:0]};  // Bit_Extender bit_extender_1
  Multiplexer #(.select(2), .width(4)) multiplexer_3 (
    .in0(4'b0001), .in1(4'b0010), .in2(4'b0100), .in3(4'b1000), .out(sb_mask), .sel(MemAddress[1:0]));
  Multiplexer #(.select(2), .width(4)) multiplexer_4 (
    .in0(4'b0011), .in2(4'b1100), .out(sh_mask), .sel(MemAddress[1:0]));  // open: in1, in3
  Comparator #(.width(7)) comparator_1 (.a(7'b0100011), .b(Instruction[6:0]), .eq(comparator_1_eq));  // open: gt, lt
  Comparator #(.width(3)) comparator_2 (.a(3'b000), .b(Instruction[14:12]), .eq(comparator_2_eq));  // open: gt, lt
  Comparator #(.width(7)) comparator_3 (.a(7'b0100011), .b(Instruction[6:0]), .eq(comparator_3_eq));  // open: gt, lt
  Comparator #(.width(3)) comparator_4 (.a(3'b001), .b(Instruction[14:12]), .eq(comparator_4_eq));  // open: gt, lt
  Comparator #(.width(7)) comparator_5 (.a(7'b0100011), .b(Instruction[6:0]), .eq(comparator_5_eq));  // open: gt, lt
  Comparator #(.width(3)) comparator_6 (.a(3'b010), .b(Instruction[14:12]), .eq(comparator_6_eq));  // open: gt, lt
  assign bit_extender_2_out = {{24{1'b0}}, DataFromReg[7:0]};  // Bit_Extender bit_extender_2
  Shifter #(.width(32)) shifter_1 (.in(bit_extender_2_out), .\dist (5'b01000), .out(shifter_1_out));
  Shifter #(.width(32)) shifter_2 (.in(bit_extender_2_out), .\dist (5'b10000), .out(shifter_2_out));
  Shifter #(.width(32)) shifter_3 (.in(bit_extender_2_out), .\dist (5'b11000), .out(shifter_3_out));
  Shifter #(.width(32)) shifter_4 (.in(bit_extender_1_out), .\dist (5'b10000), .out(shifter_4_out));
  Multiplexer #(.width(32)) multiplexer_5 (
    .in0(multiplexer_1_out), .in1(Data_SH), .out(multiplexer_5_out), .sel(is_sh));
  Multiplexer #(.width(4)) multiplexer_6 (.in0(multiplexer_2_out), .in1(sh_mask), .out(multiplexer_6_out), .sel(is_sh));
  and and_1 (is_sb, comparator_1_eq, comparator_2_eq);
  and and_2 (is_sh, comparator_3_eq, comparator_4_eq);
  and and_3 (is_sw, comparator_5_eq, comparator_6_eq);
  Multiplexer #(.width(4)) multiplexer_7 (.in0(multiplexer_6_out), .in1(4'b1111), .out(MemWriteMask), .sel(is_sw));
  Multiplexer #(.select(2), .width(32)) multiplexer_8 (
    .in0(bit_extender_1_out), .in2(shifter_4_out), .out(Data_SH), .sel(MemAddress[1:0]));  // open: in1, in3
  Multiplexer #(.width(32)) multiplexer_9 (.in0(multiplexer_5_out), .in1(DataFromReg), .out(DataToMem), .sel(is_sw));
  Multiplexer #(.select(2), .width(32)) multiplexer_10 (
    .in0(bit_extender_2_out), .in1(shifter_1_out), .in2(shifter_2_out), .in3(shifter_3_out), .out(Data_SB),
    .sel(MemAddress[1:0]));

  // Other names for the same wires on the sheet: Data8[7:0] = DataFromReg[7:0]; Data16[15:0] = DataFromReg[15:0];
  //   Opcode[6:0] = Instruction[6:0]; Func3[2:0] = Instruction[14:12]; Bottom2[1:0] = MemAddress[1:0]

  // Notes on the sheet:
  //   INPUTS to your circuit
  //   DON'T CHANGE THE LOCATIONS OF THE INPUTS AND OUTPUTS!
  //   OUTPUT from your circuit
endmodule
