// Logisim project regfile.circ as structural Verilog: 1 circuit, main circuit regfile
module regfile (
  input  [4:0] ReadIndex1,
  input  [4:0] ReadIndex2,
  input  [4:0] WriteIndex,
  input  [31:0] WriteData,
  input  RegWEn,
  input  clk,
  output [31:0] ra,
  output [31:0] sp,
  output [31:0] t0,
  output [31:0] t1,
  output [31:0] t2,
  output [31:0] s0,
  output [31:0] s1,
  output [31:0] a0,
  output [31:0] ReadData1,
  output [31:0] ReadData2
);

  wire decoder_1_out1, decoder_1_out2, decoder_1_out3, decoder_1_out4, decoder_1_out5, decoder_1_out6,
       decoder_1_out7, decoder_1_out8, decoder_1_out9, decoder_1_out10, decoder_1_out11, decoder_1_out12,
       decoder_1_out13, decoder_1_out14, decoder_1_out15, decoder_1_out16, decoder_1_out17, decoder_1_out18,
       decoder_1_out19, decoder_1_out20, decoder_1_out21, decoder_1_out22, decoder_1_out23, decoder_1_out24,
       decoder_1_out25, decoder_1_out26, decoder_1_out27, decoder_1_out28, decoder_1_out29, decoder_1_out30,
       decoder_1_out31, w1, w2, w3, w4, w5, w6, w7, w8, w9, w10, w11, w12, w13, w14, w15, w16, w17, w18, w19,
       w20, w21, w22, w23, w24, w25, w26, w27, w28, w29, w30, w31;
  wire [31:0] x0, x3, x4, x11, x12, x13, x14, x15, x16, x17, x18, x19, x20, x21, x22, x23, x24, x25, x26,
       x27, x28, x29, x30, x31;

  Decoder #(.select(5)) decoder_1 (
    .out1(decoder_1_out1), .out2(decoder_1_out2), .out3(decoder_1_out3), .out4(decoder_1_out4),
    .out5(decoder_1_out5), .out6(decoder_1_out6), .out7(decoder_1_out7), .out8(decoder_1_out8),
    .out9(decoder_1_out9), .out10(decoder_1_out10), .out11(decoder_1_out11), .out12(decoder_1_out12),
    .out13(decoder_1_out13), .out14(decoder_1_out14), .out15(decoder_1_out15), .out16(decoder_1_out16),
    .out17(decoder_1_out17), .out18(decoder_1_out18), .out19(decoder_1_out19), .out20(decoder_1_out20),
    .out21(decoder_1_out21), .out22(decoder_1_out22), .out23(decoder_1_out23), .out24(decoder_1_out24),
    .out25(decoder_1_out25), .out26(decoder_1_out26), .out27(decoder_1_out27), .out28(decoder_1_out28),
    .out29(decoder_1_out29), .out30(decoder_1_out30), .out31(decoder_1_out31), .sel(WriteIndex), .en(1'b1));  // open: out0
  Register #(.width(32)) u_x0 (.D({32{1'b0}}), .en(1'b0), .clk(clk), .Q(x0));  // open: clr
  Register #(.width(32)) u_x4 (.D(WriteData), .en(w4), .clk(clk), .Q(x4));  // open: clr
  Register #(.width(32)) x8 (.D(WriteData), .en(w8), .clk(clk), .Q(s0));  // open: clr
  Register #(.width(32)) u_x12 (.D(WriteData), .en(w12), .clk(clk), .Q(x12));  // open: clr
  Register #(.width(32)) u_x16 (.D(WriteData), .en(w16), .clk(clk), .Q(x16));  // open: clr
  Register #(.width(32)) u_x20 (.D(WriteData), .en(w20), .clk(clk), .Q(x20));  // open: clr
  Register #(.width(32)) u_x24 (.D(WriteData), .en(w24), .clk(clk), .Q(x24));  // open: clr
  Register #(.width(32)) u_x28 (.D(WriteData), .en(w28), .clk(clk), .Q(x28));  // open: clr
  Register #(.width(32)) x1 (.D(WriteData), .en(w1), .clk(clk), .Q(ra));  // open: clr
  Register #(.width(32)) x5 (.D(WriteData), .en(w5), .clk(clk), .Q(t0));  // open: clr
  Register #(.width(32)) x9 (.D(WriteData), .en(w9), .clk(clk), .Q(s1));  // open: clr
  Register #(.width(32)) u_x13 (.D(WriteData), .en(w13), .clk(clk), .Q(x13));  // open: clr
  Register #(.width(32)) u_x17 (.D(WriteData), .en(w17), .clk(clk), .Q(x17));  // open: clr
  Register #(.width(32)) u_x21 (.D(WriteData), .en(w21), .clk(clk), .Q(x21));  // open: clr
  Register #(.width(32)) u_x25 (.D(WriteData), .en(w25), .clk(clk), .Q(x25));  // open: clr
  Register #(.width(32)) u_x29 (.D(WriteData), .en(w29), .clk(clk), .Q(x29));  // open: clr
  Register #(.width(32)) x2 (.D(WriteData), .en(w2), .clk(clk), .Q(sp));  // open: clr
  Register #(.width(32)) x6 (.D(WriteData), .en(w6), .clk(clk), .Q(t1));  // open: clr
  Register #(.width(32)) x10 (.D(WriteData), .en(w10), .clk(clk), .Q(a0));  // open: clr
  Register #(.width(32)) u_x14 (.D(WriteData), .en(w14), .clk(clk), .Q(x14));  // open: clr
  Register #(.width(32)) u_x18 (.D(WriteData), .en(w18), .clk(clk), .Q(x18));  // open: clr
  Register #(.width(32)) u_x22 (.D(WriteData), .en(w22), .clk(clk), .Q(x22));  // open: clr
  Register #(.width(32)) u_x26 (.D(WriteData), .en(w26), .clk(clk), .Q(x26));  // open: clr
  Register #(.width(32)) u_x30 (.D(WriteData), .en(w30), .clk(clk), .Q(x30));  // open: clr
  Register #(.width(32)) u_x3 (.D(WriteData), .en(w3), .clk(clk), .Q(x3));  // open: clr
  Register #(.width(32)) x7 (.D(WriteData), .en(w7), .clk(clk), .Q(t2));  // open: clr
  Register #(.width(32)) u_x11 (.D(WriteData), .en(w11), .clk(clk), .Q(x11));  // open: clr
  Register #(.width(32)) u_x15 (.D(WriteData), .en(w15), .clk(clk), .Q(x15));  // open: clr
  Register #(.width(32)) u_x19 (.D(WriteData), .en(w19), .clk(clk), .Q(x19));  // open: clr
  Register #(.width(32)) u_x27 (.D(WriteData), .en(w27), .clk(clk), .Q(x27));  // open: clr
  and and_1 (w1, decoder_1_out1, RegWEn);
  and and_2 (w2, decoder_1_out2, RegWEn);
  and and_3 (w3, decoder_1_out3, RegWEn);
  and and_4 (w4, decoder_1_out4, RegWEn);
  and and_5 (w5, decoder_1_out5, RegWEn);
  and and_6 (w6, decoder_1_out6, RegWEn);
  and and_7 (w7, decoder_1_out7, RegWEn);
  and and_8 (w8, decoder_1_out8, RegWEn);
  and and_9 (w9, decoder_1_out9, RegWEn);
  and and_10 (w10, decoder_1_out10, RegWEn);
  and and_11 (w11, decoder_1_out11, RegWEn);
  and and_12 (w12, decoder_1_out12, RegWEn);
  and and_13 (w13, decoder_1_out13, RegWEn);
  and and_14 (w14, decoder_1_out14, RegWEn);
  and and_15 (w15, decoder_1_out15, RegWEn);
  and and_16 (w16, decoder_1_out16, RegWEn);
  and and_17 (w17, decoder_1_out17, RegWEn);
  and and_18 (w18, decoder_1_out18, RegWEn);
  and and_19 (w19, decoder_1_out19, RegWEn);
  and and_20 (w20, decoder_1_out20, RegWEn);
  and and_21 (w21, decoder_1_out21, RegWEn);
  and and_22 (w22, decoder_1_out22, RegWEn);
  and and_23 (w23, decoder_1_out23, RegWEn);
  and and_24 (w24, decoder_1_out24, RegWEn);
  and and_25 (w25, decoder_1_out25, RegWEn);
  and and_26 (w26, decoder_1_out26, RegWEn);
  and and_27 (w27, decoder_1_out27, RegWEn);
  and and_28 (w28, decoder_1_out28, RegWEn);
  and and_29 (w29, decoder_1_out29, RegWEn);
  and and_30 (w30, decoder_1_out30, RegWEn);
  and and_31 (w31, decoder_1_out31, RegWEn);
  Register #(.width(32)) u_x23 (.D(WriteData), .en(w23), .clk(clk), .Q(x23));  // open: clr
  Register #(.width(32)) u_x31 (.D(WriteData), .en(w31), .clk(clk), .Q(x31));  // open: clr
  Multiplexer #(.select(5), .width(32)) multiplexer_1 (
    .in0(x0), .in1(ra), .in2(sp), .in3(x3), .in4(x4), .in5(t0), .in6(t1), .in7(t2), .in8(s0), .in9(s1),
    .in10(a0), .in11(x11), .in12(x12), .in13(x13), .in14(x14), .in15(x15), .in16(x16), .in17(x17),
    .in18(x18), .in19(x19), .in20(x20), .in21(x21), .in22(x22), .in23(x23), .in24(x24), .in25(x25),
    .in26(x26), .in27(x27), .in28(x28), .in29(x29), .in30(x30), .in31(x31), .out(ReadData1), .sel(ReadIndex1));
  Multiplexer #(.select(5), .width(32)) multiplexer_2 (
    .in0(x0), .in1(ra), .in2(sp), .in3(x3), .in4(x4), .in5(t0), .in6(t1), .in7(t2), .in8(s0), .in9(s1),
    .in10(a0), .in11(x11), .in12(x12), .in13(x13), .in14(x14), .in15(x15), .in16(x16), .in17(x17),
    .in18(x18), .in19(x19), .in20(x20), .in21(x21), .in22(x22), .in23(x23), .in24(x24), .in25(x25),
    .in26(x26), .in27(x27), .in28(x28), .in29(x29), .in30(x30), .in31(x31), .out(ReadData2), .sel(ReadIndex2));

  // Notes on the sheet:
  //   INPUTS to your circuit
  //   DON'T CHANGE THE LOCATIONS OF THE INPUTS AND OUTPUTS!
  //   These are DEBUG/TEST outputs from your circuit.
  //   OUTPUTS from your circuit
endmodule
